// Logisim project Crc_4bits_teste.circ as structural Verilog: 3 circuits, main circuit crc
module crc (
  input  in_1,
  input  in_2,
  input  [4:0] Polinomio,
  output [3:0] out_4,
  output E
);

  wire and_1_out, clk, or_1_out, sc0, sc1, sc2, sc3, sc4, undriven;

  ROM #(.addrWidth(4), .dataWidth(1)) rom_1 (.addr(out_4));  // open: data
  cont15 cont15_1 (
    .rst(in_2), .start_cont(in_1), .clk(clk), .c0(out_4[0]), .c1(out_4[1]), .c2(out_4[2]), .c3(out_4[3]));
  pt1_crc c0 (
    .Reset(in_2), .Dado(undriven), .Clock(clk), .Entrada(sc3), .Poli(Polinomio[0]), .Saida(sc0));  // open: sXOR
  and and_1 (and_1_out, out_4[0], out_4[1], out_4[2], out_4[3]);
  or or_1 (or_1_out, sc0, sc1, sc2, sc3);
  and and_2 (E, or_1_out, and_1_out);
  pt1_crc c1 (.Reset(in_2), .Dado(sc0), .Clock(clk), .Entrada(sc3), .Poli(Polinomio[1]), .Saida(sc1));  // open: sXOR
  pt1_crc c2 (.Reset(in_2), .Dado(sc1), .Clock(clk), .Entrada(sc3), .Poli(Polinomio[2]), .Saida(sc2));  // open: sXOR
  pt1_crc c3 (.Reset(in_2), .Dado(sc2), .Clock(clk), .Entrada(sc3), .Poli(Polinomio[3]), .Saida(sc3));  // open: sXOR
  pt1_crc pt1_crc_1 (
    .Reset(in_2), .Dado(sc3), .Clock(clk), .Entrada(sc3), .Poli(Polinomio[4]), .Saida(sc4));  // open: sXOR

  // Other names for the same wires on the sheet: Cont[3:0] = out_4; reset = in_2; start = in_1

  // Notes on the sheet:
  //   contents of rom_1 (hex, n*v repeats v):
  //   1 0 1 0 1 0 1 0 0 1 1
endmodule

module pt1_crc (
  input  Entrada,
  input  Dado,
  input  Clock,
  input  Poli,
  input  Reset,
  output sXOR,
  output Saida
);

  wire and_1_out, and_2_out, xor_1_out;

  and and_1 (and_1_out, ~Entrada, Dado);  // AND_Gate
  xor xor_1 (xor_1_out, Dado, Poli);
  and and_2 (and_2_out, Entrada, xor_1_out);
  or or_1 (sXOR, and_1_out, and_2_out);
  D_Flip_Flop d_ff_1 (.D(sXOR), .clk(Clock), .Q(Saida), .reset(Reset));  // open: Qn, preset
endmodule

module cont15 (
  input  rst,
  input  start_cont,
  output clk,
  output c0,
  output c1,
  output c2,
  output c3
);

  wire clock_1_out, nand_1_out;

  and and_1 (clk, start_cont, clock_1_out, nand_1_out);
  Clock clock_1 (.out(clock_1_out));
  Counter #(.width(4), .max('hf)) counter_1 (
    .clr(rst), .clk(clk), .Q({c3, c2, c1, c0}));  // open: load, up, count, D, carry
  nand nand_1 (nand_1_out, c0, c1, c2, c3);
endmodule
