// Logisim project crc_8bits.circ as structural Verilog: 5 circuits, main circuit erro
module erro (
  input  c0,
  input  c1,
  input  c2,
  input  c3,
  input  c4,
  input  c5,
  input  c6,
  input  c7,
  input  [8:0] in_9,
  output erro
);

  wire and_1_out, or_1_out, or_2_out, or_3_out;

  and and_1 (and_1_out, in_9[0], in_9[1], in_9[2], in_9[3], in_9[4], in_9[5], in_9[6], in_9[7], in_9[8]);
  or or_1 (or_1_out, c0, c1, c2, c3);
  or or_2 (or_2_out, c4, c5, c6, c7);
  or or_3 (or_3_out, or_1_out, or_2_out);
  and and_2 (erro, or_3_out, and_1_out);
endmodule

module comp_op (
  input  Cn,
  input  Dado,
  input  clk,
  input  Pn,
  input  rst,
  output cn1
);

  wire and_1_out, and_2_out, or_1_out, xor_1_out;

  and and_1 (and_1_out, ~Cn, Dado);  // AND_Gate
  xor xor_1 (xor_1_out, Dado, Pn);
  and and_2 (and_2_out, Cn, xor_1_out);
  or or_1 (or_1_out, and_1_out, and_2_out);
  D_Flip_Flop d_ff_1 (.D(or_1_out), .clk(clk), .Q(cn1), .reset(rst));  // open: Qn, preset
endmodule

module n508 (
  input  c0,
  input  c1,
  input  c2,
  input  c3,
  input  c4,
  input  c5,
  input  c6,
  input  c7,
  input  c8,
  output stop
);

  wire and_1_out;

  and and_1 (and_1_out, ~c0, ~c1, c2, c3, c4, c5, c6, c7, c8);  // AND_Gate
  not not_1 (stop, and_1_out);
endmodule

module cont508 (
  input  strt,
  input  rst,
  output clk,
  output [8:0] cont
);

  wire clock_1_out, nao508;

  and and_1 (clk, strt, clock_1_out, nao508);
  Clock clock_1 (.out(clock_1_out));
  Counter #(.width(9), .max('h1ff)) counter_1 (.clr(rst), .clk(clk), .Q(cont));  // open: load, up, count, D, carry
  n508 n508_1 (
    .c0(cont[0]), .c1(cont[1]), .c2(cont[2]), .c3(cont[3]), .c4(cont[4]), .c5(cont[5]), .c6(cont[6]),
    .c7(cont[7]), .c8(cont[8]), .stop(nao508));

  // Other names for the same wires on the sheet: reset = rst; start = strt
endmodule

module crc8bits (
);

  wire comp_op_1_cn1, comp_op_2_cn1, comp_op_3_cn1, comp_op_4_cn1, comp_op_5_cn1, comp_op_6_cn1,
       comp_op_7_cn1, undriven;

  ROM #(.addrWidth(9), .dataWidth(1)) rom_1 ();  // open: addr, data
  cont508 cont508_1 ();  // open: strt, rst, clk, cont
  comp_op comp_op_1 (.Cn(undriven), .cn1(comp_op_1_cn1));  // open: rst, Pn, clk, Dado
  comp_op comp_op_2 (.Cn(comp_op_1_cn1), .cn1(comp_op_2_cn1));  // open: rst, Pn, clk, Dado
  comp_op comp_op_3 (.Cn(comp_op_2_cn1), .cn1(comp_op_3_cn1));  // open: rst, Pn, clk, Dado
  comp_op comp_op_4 (.Cn(comp_op_3_cn1), .cn1(comp_op_4_cn1));  // open: rst, Pn, clk, Dado
  comp_op comp_op_5 (.Cn(comp_op_4_cn1), .cn1(comp_op_5_cn1));  // open: rst, Pn, clk, Dado
  comp_op comp_op_6 (.Cn(comp_op_5_cn1), .cn1(comp_op_6_cn1));  // open: rst, Pn, clk, Dado
  comp_op comp_op_7 (.Cn(comp_op_6_cn1), .cn1(comp_op_7_cn1));  // open: rst, Pn, clk, Dado
  comp_op comp_op_8 (.Cn(comp_op_7_cn1));  // open: rst, Pn, clk, Dado, cn1
endmodule
